# Fritzing sketch Banba mmotors (saved by Fritzing 0.9.3b)
breadboards: 1

parts:
  Part1 = Arduino Nano 33 IOT
  IC1 = H-Bridge [package=THT]
  M1 = DC Motor
  M2 = DC Motor

nets:
  GND: Part1.GND, IC1.GND1, IC1.GND2, IC1.GND3, IC1.GND4
  N1: Part1.D5~, IC1.3A
  N2: Part1.D6~, IC1.4A
  N3: Part1.D9~, IC1.1A
  N4: Part1.D10~, IC1.2A
  N5: Part1.+5V, IC1.1_2EN, IC1.VCC2, IC1.3_4EN, IC1.VCC1
  N6: IC1.1Y, M2.pin_1
  N7: IC1.2Y, M2.pin_2
  N8: IC1.3Y, M1.pin_2
  N9: IC1.4Y, M1.pin_1

custom parts:
  Arduino Nano 33 IOT: The Arduino Nano 33 IoT is the easiest and cheapest point of entry to enhance existing devices (and creating new ones) to be part of the IoT and designing pico-network applications. Whether you are looking at building a sensor network connected to your office or home router, or if you want to create a BLE device sending data to a cellphone, the Nano 33 IoT is your one-stop-solution for many of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
